// Digital circuit project.dig as structural Verilog
module project (
  input  in_1,
  input  clk,
  output [6:0] out_3,
  output [15:0] out_4
);

  wire _0_out, _1_out, _2_out, _3_out, _4_out, _5_out, _6_out, _7_out, _8_out, _9_out, and_1_out, and_2_out,
       ID_2_out, PASS_2_out, u_encoder_da, u_mode_selector_id0, u_mode_selector_pwd0, u_shifter_pwd_led1,
       u_shifter_pwd_led2, u_shifter_pwd_led3, u_shifter_pwd_led4, u_shifter_pwd_match, u_timer_dis,
       u_timer_reset;
  wire [3:0] u_encoder_data, u_shifter_id0, u_shifter_id1;

  Button _1 (.out(_1_out));
  Button _4 (.out(_4_out));
  Button _7 (.out(_7_out));
  Button _2 (.out(_2_out));
  Button _5 (.out(_5_out));
  Button _8 (.out(_8_out));
  Button _0 (.out(_0_out));
  Button _3 (.out(_3_out));
  Button _6 (.out(_6_out));
  Button _9 (.out(_9_out));
  LED ID (.in(u_mode_selector_id0));
  LED PASS (.in(u_mode_selector_pwd0));
  Button ID_2 (.out(ID_2_out));
  Button PASS_2 (.out(PASS_2_out));
  mode_selector #(.applicationType("IVERILOG")) u_mode_selector (
    .ID(ID_2_out), .PWD(PASS_2_out), .DIS(u_timer_dis), .RESET(u_timer_reset), .CLK(clk), .RST(in_1),
    .ID0(u_mode_selector_id0), .PWD0(u_mode_selector_pwd0));
  encoder #(.applicationType("IVERILOG")) u_encoder (
    .P0(_0_out), .P1(_1_out), .P2(_2_out), .P3(_3_out), .P4(_4_out), .P5(_5_out), .P6(_6_out), .P7(_7_out),
    .P8(_8_out), .P9(_9_out), .CLK(clk), .RST(in_1), .DATA(u_encoder_data), .DA(u_encoder_da));
  ROM #(.AddrBits(7), .Bits(16)) Password (.A(out_3), .sel(1'b1), .D(out_4));
  timer #(.applicationType("IVERILOG")) u_timer (
    .START(u_shifter_pwd_led4), .CLK(clk), .RST(in_1), .RESET(u_timer_reset), .DIS(u_timer_dis));
  shifter #(.applicationType("IVERILOG")) u_shifter (
    .IN(u_encoder_data), .EN(u_mode_selector_id0), .DA(u_encoder_da), .CLK(clk), .RST(in_1),
    .ID0(u_shifter_id0), .ID1(u_shifter_id1), .HEX(out_3));
  shifter_pwd #(.applicationType("IVERILOG")) u_shifter_pwd (
    .DATAIN(u_encoder_data), .PWDIN(out_4), .EN(u_mode_selector_pwd0), .DA(u_encoder_da), .CLK(clk),
    .RST(in_1), .MATCH(u_shifter_pwd_match), .LED1(u_shifter_pwd_led1), .LED2(u_shifter_pwd_led2),
    .LED3(u_shifter_pwd_led3), .LED4(u_shifter_pwd_led4));
  Seven_Seg_Hex seven_seg_hex_1 (.d(u_shifter_id0), .dp(1'b0));
  Seven_Seg_Hex seven_seg_hex_2 (.d(u_shifter_id1), .dp(1'b0));
  LED led_1 (.in(u_shifter_pwd_led1));
  LED led_2 (.in(u_shifter_pwd_led2));
  and and_1 (and_1_out, u_shifter_pwd_match, u_shifter_pwd_led4);
  and and_2 (and_2_out, ~u_shifter_pwd_match, u_shifter_pwd_led4);  // And
  LED led_3 (.in(u_shifter_pwd_led3));
  LED led_4 (.in(u_shifter_pwd_led4));
  LED GRANTED (.in(and_1_out));
  LED DENIED (.in(and_2_out));

  // Notes on the sheet:
  //   clk: Hz: 100
  //   Nida Kayaduman
  //   contents of Password (hex, n*v repeats v):
  //   1234,5678,33*ffff,1919,63*ffff
endmodule

/* Code of mode_selector:
module mode_selector(
    input ID, PWD, DIS, RESET, CLK, RST,
    output reg ID0, PWD0
);
    
    initial begin
        ID0 = 1'b1; 
        PWD0 = 1'b0;
    end

    always @(posedge CLK or negedge RST) begin
        if (!RST) begin
            ID0 <= 1'b1; 
            PWD0 <= 1'b0;
        end else begin
            if (DIS) begin
                ID0 <= 1'b1; 
                PWD0 <= 1'b0;
            end else if (ID) begin
                ID0 <= 1'b1;
                PWD0 <= 1'b0;
            end else if (PWD) begin
                ID0 <= 1'b0;
                PWD0 <= 1'b1;
            end
        end
    end
endmodule
*/

/* Code of encoder:
module encoder(
	input P0, P1, P2, P3, P4, P5, P6, P7, P8, P9,
	input CLK, RST,
	output reg [3:0] DATA,
	output reg DA);
	
	reg pressed;
	wire button;

	assign button = P0|P1|P2|P3|P4|P5|P6|P7|P8|P9;

	always @(posedge CLK, negedge RST) 
		if(~RST)
		begin
			pressed <= 0;
			DATA <= 4'b0000;
		end
		else
		begin
			if(button)
			begin
				if(~pressed)
				begin
					pressed <= 1'b1;
					DA <= 1'b1;
				end
				else
					DA <= 1'b0;
				if      (P0) DATA <= 4'b0000;
				else if (P1) DATA <= 4'b0001;
				else if (P2) DATA <= 4'b0010;
				else if (P3) DATA <= 4'b0011;
				else if (P4) DATA <= 4'b0100;
				else if (P5) DATA <= 4'b0101;
				else if (P6) DATA <= 4'b0110;
				else if (P7) DATA <= 4'b0111;
				else if (P8) DATA <= 4'b1000;
				else         DATA <= 4'b1001;
			end
			else
			begin
				pressed <= 1'b0;
				DA <= 1'b0;
			end				
		end			
endmodule
*/

/* Code of timer:
module timer(
    input START, CLK, RST,
    output reg RESET, DIS
);

    
    reg [8:0] count;

    
    initial begin
        count = 9'b0;
        DIS = 1'b0;
        RESET = 1'b0;
    end


    always @(posedge CLK) begin
        if (!RST || RESET) begin 
            count <= 9'b0;
            DIS <= 1'b0;

            RESET <= 1'b0;
        end else if (START && count != 9'b100101100) begin 
            count <= count + 9'b1;
            DIS <= 1'b0;
            RESET <= 1'b0;
        end else if (count == 9'b100101100) begin 
            count <= 9'b0;
            DIS <= 1'b1;
            RESET <= 1'b1;
        end
    end
endmodule
*/

/* Code of shifter:
module shifter (
  input wire [3:0] IN,
  input wire EN,
  input wire DA,
  input wire CLK,
  input wire RST,
  output reg [3:0] ID0,  
  output reg [3:0] ID1,  
  output reg [6:0] HEX
);

  reg [7:0] binary;
  reg [3:0] hex_table [0:15]; 

  initial begin
   
    hex_table[4'b0000] = 4'b0000;  // 0
    hex_table[4'b0001] = 4'b0001;  // 1
    hex_table[4'b0010] = 4'b0010;  // 2
    hex_table[4'b0011] = 4'b0011;  // 3
    hex_table[4'b0100] = 4'b0100;  // 4
    hex_table[4'b0101] = 4'b0101;  // 5
    hex_table[4'b0110] = 4'b0110;  // 6
    hex_table[4'b0111] = 4'b0111;  // 7
    hex_table[4'b1000] = 4'b1000;  // 8
    hex_table[4'b1001] = 4'b1001;  // 9
    hex_table[4'b1010] = 4'b1010;  // A
    hex_table[4'b1011] = 4'b1011;  // B
    hex_table[4'b1100] = 4'b1100;  // C
    hex_table[4'b1101] = 4'b1101;  // D
    hex_table[4'b1110] = 4'b1110;  // E
    hex_table[4'b1111] = 4'b1111;  // F

    
    ID0 <= 4'b0000;
    ID1 <= 4'b0000;
    HEX <= 7'b0000000;
  end

  always @(posedge CLK or negedge RST) begin
    if (!RST) begin
      ID0 <= 4'b0000;
      ID1 <= 4'b0000;
      HEX <= 7'b0000000;
    end else if (EN) begin
      if (DA) begin
        ID0 <= ID1;
        ID1 <= IN;
      end
      binary = ID0 * 10 + ID1;  
      HEX <= {hex_table[binary[7:4]], hex_table[binary[3:0]], 1'b0}/2; 
    end
  end
endmodule
*/

/* Code of shifter_pwd:
module shifter_pwd (
    input wire [3:0] DATAIN,
    input wire [15:0] PWDIN,
    input wire EN,
    input wire DA,
    input wire CLK,
    input wire RST,
    output reg MATCH,
    output reg LED1,
    output reg LED2,
    output reg LED3,
    output reg LED4
);

    reg [15:0] data;
    reg [15:0] rom_data;
    reg [1:0] input_counter;

    always @(posedge CLK or negedge RST) begin
        if (!RST) begin
            data <= 16'b0;
            rom_data <= 16'b0;
            input_counter <= 2'b0;
            {LED1, LED2, LED3, LED4, MATCH} <= 5'b0;
        end else if (EN && DA) begin
            case (input_counter)
                2'b00: begin
                    data[15:12] <= DATAIN;
                    rom_data[15:12] <= PWDIN[15:12];
                    LED1 <= 1'b1;
                end
                2'b01: begin
                    data[11:8] <= DATAIN;
                    rom_data[11:8] <= PWDIN[11:8];
                    LED2 <= 1'b1;
                end
                2'b10: begin
                    data[7:4] <= DATAIN;
                    rom_data[7:4] <= PWDIN[7:4];
                    LED3 <= 1'b1;
                end
                2'b11: begin
                    data[3:0] <= DATAIN;
                    rom_data[3:0] <= PWDIN[3:0];
                    LED4 <= 1'b1;
                    MATCH <= (data == rom_data) ? 1'b1 : 1'b0;
                    if (MATCH == 1'b1 || !EN) begin
                        data <= 16'b0;
                        rom_data <= 16'b0;
                        input_counter <= 2'b0;
                        {LED1, LED2, LED3, LED4} <= 4'b0;
                        MATCH <= 1'b0;  
                    end
                end
            endcase
            if (input_counter != 2'b11) begin
                input_counter <= input_counter + 1'b1;
            end
        end

        if (!EN) begin
            data <= 16'b0;
            rom_data <= 16'b0;
            input_counter <= 2'b0;
            {LED1, LED2, LED3, LED4} <= 4'b0;
            MATCH <= 1'b0;  
        end
    end
endmodule
*/
